# Fritzing sketch esquema_hardware (saved by Fritzing 0.9.3b)
breadboards: 1

parts:
  BATT1 = LiPoly Battery (1300mAh) [part_number=as]
  Part1 = Arduino Uno (Rev3)
  Raspberry_Pi_1 = Raspberry Pi 3 [part_number=RPI-3-V1.2]
  BATT2 = LiPoly Battery (1300mAh) [part_number=as]
  BATT3 = LiPoly Battery (1300mAh) [part_number=as]
  U1 = TRANSCHIPTC5747 [package=camera_sfv24r-2st_2]  # not connected
  Part4 = Tri-Axis Gyro Breakout - L3G4200D
  IC1 = ULN2003A [package="DIP16 [THT]"]
  IC2 = ULN2003A [package="DIP16 [THT]"]
  IC3 = ULN2003A [package="DIP16 [THT]"]
  USBTTL2 = USB A Plug
  USBTTL3 = Micro USB B Plug
  M2 = Stepper Motor - Unipolar
  M1 = Stepper Motor - Unipolar
  M3 = Stepper Motor - Unipolar

nets:
  N1: BATT1.positive, Part1.VIN
  N2: BATT1.negative, Part1.GND
  N3: Part1.D8, IC2.In_1
  N4: Part1.D9_PWM, IC2.In_2
  N5: Part1.D10_PWM/SS, Part1.D12/MISO, IC1.In_3
  N6: Part1.D11_PWM/MOSI, IC1.In_2
  N7: Part1.D13/SCK, IC1.In_1
  N8: Part1.D2, IC3.In_4
  N9: Part1.D3_PWM, IC3.In_3
  N10: Part1.D4, IC3.In_1
  N11: Part1.D5_PWM, IC3.In_2
  N12: Part1.D6_PWM, IC2.In_3
  N13: Part1.D7, IC2.In_4
  3V3: Raspberry_Pi_1.3v3, Part4.VCC
  N14: Raspberry_Pi_1.GPIO2, Part4.SCL
  N15: Raspberry_Pi_1.GPIO3, Part4.SDA
  GND: Raspberry_Pi_1.GND, BATT2.negative, Part4.GND
  N16: Raspberry_Pi_1.5V, BATT2.positive
  N17: BATT3.positive, IC1.COM_-_Common, IC2.COM_-_Common, IC3.COM_-_Common, M2.COMMON_1, M1.COMMON_1
  N18: BATT3.negative, IC1.0V, IC2.0V, IC3.0V
  N19: IC1.Out_4, M1.A
  N20: IC1.Out_3, M1.C
  N21: IC1.Out_2, M1.B
  N22: IC1.Out_1, M1.D
  N23: IC2.Out_4, M3.A
  N24: IC2.Out_3, M3.C
  N25: IC2.Out_2, M3.B
  N26: IC2.Out_1, M3.D
  N27: IC3.Out_4, M2.A
  N28: IC3.Out_3, M2.C
  N29: IC3.Out_2, M2.B
  N30: IC3.Out_1, M2.D
  N31: USBTTL2.usb, USBTTL3.usb

custom parts:
  LiPoly Battery (1300mAh): Lithium Ion Polymer Battery (1300mAh)
